// Logisim project datapath.circ as structural Verilog: 3 circuits, main circuit main
module main (
  input  EnteringCodeSignal,
  input  EnteringGuessSignal,
  input  KeyPress,
  input  DoneGuessingSignal,
  input  [3:0] Number,
  input  in_6,
  output [3:0] GT,
  output Win,
  output [3:0] EQ,
  output [3:0] LT
);

  wire and_1_out, and_2_out, and_3_out, and_4_out, and_5_out, and_6_out, and_7_out, and_8_out, clock_1_out,
       decoder_1_out0, decoder_1_out1, decoder_1_out2, decoder_1_out3;
  wire [1:0] guessCounter_q, numberCounter_q;
  wire [3:0] code1_q, code2_q, code3_q, code4_q, comparator_4_eq, comparator_4_gt, comparator_4_lt, guess1_q,
       guess2_q, guess3_q, guess4_q, undriven;

  Clock clock_1 (.out(clock_1_out));
  Decoder #(.enable("false"), .select(2)) decoder_1 (
    .out0(decoder_1_out0), .out1(decoder_1_out1), .out2(decoder_1_out2), .out3(decoder_1_out3),
    .sel(numberCounter_q));
  Counter #(.max('h3), .width(2)) numberCounter (
    .count(KeyPress), .Q(numberCounter_q), .clk(clock_1_out));  // open: load, D, carry, clr
  and and_1 (and_1_out, EnteringCodeSignal, decoder_1_out0);
  and and_2 (and_2_out, EnteringCodeSignal, decoder_1_out1);
  and and_3 (and_3_out, EnteringCodeSignal, decoder_1_out2);
  and and_4 (and_4_out, EnteringCodeSignal, decoder_1_out3);
  Register #(.width(4)) code1 (.en(and_1_out), .Q(code1_q));  // open: D, clk, clr
  Register #(.width(4)) code2 (.D(undriven), .en(and_2_out), .Q(code2_q));  // open: clk, clr
  Register #(.width(4)) code3 (.D(undriven), .en(and_3_out), .Q(code3_q));  // open: clk, clr
  Register #(.width(4)) code4 (.D(undriven), .en(and_4_out), .Q(code4_q));  // open: clk, clr
  Register #(.width(4)) guess1 (.D(Number), .en(and_5_out), .Q(guess1_q));  // open: clk, clr
  and and_5 (and_5_out, EnteringGuessSignal, decoder_1_out0);
  Register #(.width(4)) guess2 (.D(Number), .en(and_6_out), .Q(guess2_q));  // open: clk, clr
  and and_6 (and_6_out, EnteringGuessSignal, decoder_1_out1);
  Register #(.width(4)) guess3 (.D(Number), .en(and_7_out), .Q(guess3_q));  // open: clk, clr
  and and_7 (and_7_out, EnteringGuessSignal, decoder_1_out2);
  Register #(.width(4)) guess4 (.D(Number), .en(and_8_out), .Q(guess4_q));  // open: clk, clr
  and and_8 (and_8_out, EnteringGuessSignal, decoder_1_out3);
  Comparator #(.mode("unsigned"), .width(4)) comparator_1 (
    .a(code1_q), .b(guess1_q), .gt(comparator_4_gt[3]), .eq(comparator_4_eq[3]), .lt(comparator_4_lt[3]));
  Comparator #(.mode("unsigned"), .width(4)) comparator_2 (
    .a(code2_q), .b(guess2_q), .gt(comparator_4_gt[2]), .eq(comparator_4_eq[2]), .lt(comparator_4_lt[2]));
  Comparator #(.mode("unsigned"), .width(4)) comparator_3 (
    .a(code3_q), .b(guess3_q), .gt(comparator_4_gt[1]), .eq(comparator_4_eq[1]), .lt(comparator_4_lt[1]));
  Comparator #(.mode("unsigned"), .width(4)) comparator_4 (
    .a(code4_q), .b(guess4_q), .gt(comparator_4_gt[0]), .eq(comparator_4_eq[0]), .lt(comparator_4_lt[0]));
  Multiplexer #(.enable("false"), .width(4)) multiplexer_1 (
    .in0(4'b0000), .in1(comparator_4_gt), .out(GT), .sel(DoneGuessingSignal));
  Multiplexer #(.enable("false"), .width(4)) multiplexer_2 (
    .in0(4'b0000), .in1(comparator_4_eq), .out(EQ), .sel(DoneGuessingSignal));
  Multiplexer #(.enable("false"), .width(4)) multiplexer_3 (
    .in0(4'b0000), .in1(comparator_4_lt), .out(LT), .sel(DoneGuessingSignal));
  Counter #(.max('h3), .width(2)) guessCounter (
    .count(DoneGuessingSignal), .Q(guessCounter_q));  // open: load, D, carry, clk, clr
  Comparator #(.mode("unsigned"), .width(2)) comparator_5 (.a(guessCounter_q));  // open: b, gt, eq, lt
  Comparator #(.mode("unsigned"), .width(4)) comparator_6 (.a(4'b1111), .b(EQ), .eq(Win));  // open: gt, lt
endmodule

module datapath (
  input  ResetSignal,
  input  CheckSignal,
  input  EnteringCodeSignal,
  input  KeyPress,
  input  [3:0] Number,
  input  EnteringGuessSignal,
  output [3:0] GT,
  output [3:0] EQ,
  output WinSignal,
  output [3:0] LT,
  output NumberCountTC,
  output GuessCountTC
);

  wire and_1_out, and_2_out, and_3_out, clock_1_out;
  wire [3:0] cod2_q, code1_q, code3_q, code4_q, comparator_1_eq, comparator_1_gt, comparator_1_lt, guess1_q,
       guess2_q, guess3_q, guess4_q;

  Clock clock_1 (.out(clock_1_out));
  and and_1 (and_1_out, EnteringCodeSignal, KeyPress);
  and and_2 (and_2_out, KeyPress, EnteringGuessSignal);
  and and_3 (and_3_out, NumberCountTC, EnteringGuessSignal);
  Register #(.width(4)) code4 (.D(Number), .en(and_1_out), .Q(code4_q), .clk(clock_1_out), .clr(ResetSignal));
  Comparator #(.mode("unsigned"), .width(4)) comparator_1 (
    .a(code4_q), .b(guess4_q), .gt(comparator_1_gt[0]), .eq(comparator_1_eq[0]), .lt(comparator_1_lt[0]));
  Register #(.width(4)) guess4 (.D(Number), .en(and_2_out), .Q(guess4_q), .clk(clock_1_out), .clr(ResetSignal));
  Counter #(.max('h3), .width(2)) numberCounter (
    .count(KeyPress), .carry(NumberCountTC), .clk(clock_1_out), .clr(ResetSignal));  // open: load, D, Q
  Counter #(.max('h3), .width(2)) guessCounter (
    .count(and_3_out), .carry(GuessCountTC), .clk(clock_1_out), .clr(ResetSignal));  // open: load, D, Q
  Register #(.width(4)) code3 (.D(code4_q), .en(and_1_out), .Q(code3_q), .clk(clock_1_out), .clr(ResetSignal));
  Register #(.width(4)) cod2 (.D(code3_q), .en(and_1_out), .Q(cod2_q), .clk(clock_1_out), .clr(ResetSignal));
  Comparator #(.mode("unsigned"), .width(4)) comparator_2 (
    .a(code3_q), .b(guess3_q), .gt(comparator_1_gt[1]), .eq(comparator_1_eq[1]), .lt(comparator_1_lt[1]));
  Register #(.width(4)) guess3 (.D(guess4_q), .en(and_2_out), .Q(guess3_q), .clk(clock_1_out), .clr(ResetSignal));
  Register #(.width(4)) guess2 (.D(guess3_q), .en(and_2_out), .Q(guess2_q), .clk(clock_1_out), .clr(ResetSignal));
  Register #(.width(4)) code1 (.D(cod2_q), .en(and_1_out), .Q(code1_q), .clk(clock_1_out), .clr(ResetSignal));
  Comparator #(.mode("unsigned"), .width(4)) comparator_3 (
    .a(cod2_q), .b(guess2_q), .gt(comparator_1_gt[2]), .eq(comparator_1_eq[2]), .lt(comparator_1_lt[2]));
  Register #(.width(4)) guess1 (.D(guess2_q), .en(and_2_out), .Q(guess1_q), .clk(clock_1_out), .clr(ResetSignal));
  Comparator #(.mode("unsigned"), .width(4)) comparator_4 (
    .a(code1_q), .b(guess1_q), .gt(comparator_1_gt[3]), .eq(comparator_1_eq[3]), .lt(comparator_1_lt[3]));
  Register #(.width(4)) GT_reg (.D(comparator_1_gt), .en(CheckSignal), .Q(GT), .clk(clock_1_out), .clr(ResetSignal));
  Register #(.width(4)) EQ_reg (.D(comparator_1_eq), .en(CheckSignal), .Q(EQ), .clk(clock_1_out), .clr(ResetSignal));
  Register #(.width(4)) LT_reg (.D(comparator_1_lt), .en(CheckSignal), .Q(LT), .clk(clock_1_out), .clr(ResetSignal));
  Comparator #(.mode("unsigned"), .width(4)) comparator_5 (.a(EQ), .b(4'b1111), .eq(WinSignal));  // open: gt, lt

  // Notes on the sheet:
  //   clk
endmodule

module datapath1 (
  input  ResetSignal,
  input  CheckSignal,
  input  EnteringCodeSignal,
  input  KeyPress,
  input  [3:0] Number,
  input  EnteringGuessSignal,
  output [3:0] GT,
  output [3:0] EQ,
  output WinSignal,
  output [3:0] LT,
  output NumberCountTC,
  output GuessCountTC
);

  wire and_1_out, and_2_out, and_3_out, clock_1_out, or_1_out;
  wire [2:0] guessCounter_q, numberCounter_q;
  wire [3:0] cod2_q, code1_q, code3_q, code4_q, comparator_1_eq, comparator_1_gt, comparator_1_lt, guess1_q,
       guess2_q, guess3_q, guess4_q;

  Clock clock_1 (.out(clock_1_out));
  and and_1 (and_1_out, EnteringCodeSignal, KeyPress);
  and and_2 (and_2_out, KeyPress, EnteringGuessSignal);
  or or_1 (or_1_out, ResetSignal, NumberCountTC);
  and and_3 (and_3_out, NumberCountTC, EnteringGuessSignal);
  Register #(.width(4)) code4 (.D(Number), .en(and_1_out), .Q(code4_q), .clk(clock_1_out), .clr(ResetSignal));
  Comparator #(.mode("unsigned"), .width(4)) comparator_1 (
    .a(code4_q), .b(guess4_q), .gt(comparator_1_gt[0]), .eq(comparator_1_eq[0]), .lt(comparator_1_lt[0]));
  Register #(.width(4)) guess4 (.D(Number), .en(and_2_out), .Q(guess4_q), .clk(clock_1_out), .clr(ResetSignal));
  Counter #(.max('h4), .width(3)) numberCounter (
    .load(or_1_out), .D(3'b000), .count(KeyPress), .Q(numberCounter_q), .clk(clock_1_out), .clr(clock_1_out));  // open: carry
  Counter #(.max('h4), .width(3)) guessCounter (
    .count(and_3_out), .Q(guessCounter_q), .clk(clock_1_out), .clr(ResetSignal));  // open: load, D, carry
  Register #(.width(4)) code3 (.D(code4_q), .en(and_1_out), .Q(code3_q), .clk(clock_1_out), .clr(ResetSignal));
  Register #(.width(4)) cod2 (.D(code3_q), .en(and_1_out), .Q(cod2_q), .clk(clock_1_out), .clr(ResetSignal));
  Comparator #(.mode("unsigned"), .width(4)) comparator_2 (
    .a(code3_q), .b(guess3_q), .gt(comparator_1_gt[1]), .eq(comparator_1_eq[1]), .lt(comparator_1_lt[1]));
  Register #(.width(4)) guess3 (.D(guess4_q), .en(and_2_out), .Q(guess3_q), .clk(clock_1_out), .clr(ResetSignal));
  Register #(.width(4)) guess2 (.D(guess3_q), .en(and_2_out), .Q(guess2_q), .clk(clock_1_out), .clr(ResetSignal));
  Comparator #(.mode("unsigned"), .width(3)) comparator_3 (
    .a(3'b100), .b(numberCounter_q), .eq(NumberCountTC));  // open: gt, lt
  Comparator #(.mode("unsigned"), .width(3)) comparator_4 (
    .a(3'b100), .b(guessCounter_q), .eq(GuessCountTC));  // open: gt, lt
  Register #(.width(4)) code1 (.D(cod2_q), .en(and_1_out), .Q(code1_q), .clk(clock_1_out), .clr(ResetSignal));
  Comparator #(.mode("unsigned"), .width(4)) comparator_5 (
    .a(cod2_q), .b(guess2_q), .gt(comparator_1_gt[2]), .eq(comparator_1_eq[2]), .lt(comparator_1_lt[2]));
  Register #(.width(4)) guess1 (.D(guess2_q), .en(and_2_out), .Q(guess1_q), .clk(clock_1_out), .clr(ResetSignal));
  Comparator #(.mode("unsigned"), .width(4)) comparator_6 (
    .a(code1_q), .b(guess1_q), .gt(comparator_1_gt[3]), .eq(comparator_1_eq[3]), .lt(comparator_1_lt[3]));
  Multiplexer #(.enable("false"), .width(4)) multiplexer_1 (
    .in0(4'b0000), .in1(comparator_1_gt), .out(GT), .sel(CheckSignal));
  Multiplexer #(.enable("false"), .width(4)) multiplexer_2 (
    .in0(4'b0000), .in1(comparator_1_eq), .out(EQ), .sel(CheckSignal));
  Multiplexer #(.enable("false"), .width(4)) multiplexer_3 (
    .in0(4'b0000), .in1(comparator_1_lt), .out(LT), .sel(CheckSignal));
  Comparator #(.mode("unsigned"), .width(4)) comparator_7 (.a(EQ), .b(4'b1111), .eq(WinSignal));  // open: gt, lt

  // Notes on the sheet:
  //   clk
endmodule
